// Logisim project 8-bit using full adder part 1.circ as structural Verilog: 1 circuit, main circuit main
module main (
  input  A0,
  input  B0,
  input  Cin,
  input  A1,
  input  B1,
  input  A2,
  input  B2,
  input  A3,
  input  B3,
  output S0,
  output C0,
  output S1,
  output C1,
  output S2,
  output C2,
  output S3,
  output C3
);

  wire nand_1_out, nand_2_out, nand_3_out, nand_4_out, nand_5_out, nand_6_out, nand_7_out, nand_8_out,
       xor_1_out, xor_2_out, xor_3_out, xor_4_out;

  xor xor_1 (xor_1_out, A0, B0);
  xor xor_2 (xor_2_out, A1, B1);
  xor xor_3 (xor_3_out, A2, B2);
  xor xor_4 (xor_4_out, A3, B3);
  nand nand_1 (nand_1_out, xor_1_out, Cin);
  nand nand_2 (nand_2_out, A0, B0);
  nand nand_3 (nand_3_out, xor_2_out, C0);
  nand nand_4 (nand_4_out, A1, B1);
  nand nand_5 (nand_5_out, xor_3_out, C1);
  nand nand_6 (nand_6_out, A2, B2);
  nand nand_7 (nand_7_out, xor_4_out, C2);
  nand nand_8 (nand_8_out, A3, B3);
  xor xor_5 (S0, xor_1_out, Cin);
  xor xor_6 (S1, xor_2_out, C0);
  xor xor_7 (S2, xor_3_out, C1);
  xor xor_8 (S3, xor_4_out, C2);
  nand nand_9 (C0, nand_1_out, nand_2_out);
  nand nand_10 (C1, nand_3_out, nand_4_out);
  nand nand_11 (C2, nand_5_out, nand_6_out);
  nand nand_12 (C3, nand_7_out, nand_8_out);
endmodule
