// Logisim project 8-bit using full adder part 2.circ as structural Verilog: 1 circuit, main circuit main
module main (
  input  A4,
  input  B4,
  input  C3,
  input  A5,
  input  B5,
  input  A6,
  input  B6,
  input  A7,
  input  B7,
  output S4,
  output C4,
  output S5,
  output C5,
  output S6,
  output C6,
  output S7,
  output C7
);

  wire nand_1_out, nand_2_out, nand_3_out, nand_4_out, nand_5_out, nand_6_out, nand_7_out, nand_8_out,
       nand_12_out, nand_13_out, xor_1_out, xor_2_out, xor_3_out, xor_4_out;

  nand nand_1 (nand_1_out, A7, B7);
  xor xor_1 (xor_1_out, A7, B7);
  xor xor_2 (xor_2_out, A4, B4);
  xor xor_3 (xor_3_out, A5, B5);
  xor xor_4 (xor_4_out, A6, B6);
  nand nand_2 (nand_2_out, nand_1_out, nand_1_out);
  nand nand_3 (nand_3_out, xor_2_out, C3);
  nand nand_4 (nand_4_out, A4, B4);
  nand nand_5 (nand_5_out, xor_3_out, C4);
  nand nand_6 (nand_6_out, A5, B5);
  nand nand_7 (nand_7_out, xor_4_out, C5);
  nand nand_8 (nand_8_out, A6, B6);
  xor xor_5 (S4, xor_2_out, C3);
  nand nand_9 (C4, nand_3_out, nand_4_out);
  xor xor_6 (S5, xor_3_out, C4);
  nand nand_10 (C5, nand_5_out, nand_6_out);
  xor xor_7 (S6, xor_4_out, C5);
  nand nand_11 (C6, nand_7_out, nand_8_out);
  xor xor_8 (S7, xor_1_out, C6);
  nand nand_12 (nand_12_out, xor_1_out, C6);
  nand nand_13 (nand_13_out, nand_12_out, nand_12_out);
  or or_1 (C7, nand_13_out, nand_2_out);
endmodule
