// Logisim project Half adder.circ as structural Verilog: 1 circuit, main circuit main
module main (
  input  A,
  input  B,
  output S,
  output C
);

  wire nand_1_out;

  nand nand_1 (nand_1_out, A, B);
  xor xor_1 (S, A, B);
  nand nand_2 (C, nand_1_out, nand_1_out);
endmodule
