// Logisim project LEDA.circ as structural Verilog: 1 circuit, main circuit main
module main (
  input  a,
  input  b,
  input  c,
  input  d,
  output x
);

  wire and_1_out, and_2_out, and_3_out, and_4_out, and_5_out, and_6_out, and_7_out, and_8_out, and_9_out,
       and_10_out, not_1_out, not_2_out, not_3_out, not_4_out, not_5_out, not_6_out, not_7_out, not_8_out,
       not_9_out, or_1_out, or_2_out, or_3_out;

  not not_1 (not_1_out, a);
  and and_1 (and_1_out, not_1_out, not_2_out);
  not not_2 (not_2_out, b);
  not not_3 (not_3_out, d);
  not not_4 (not_4_out, a);
  and and_2 (and_2_out, not_4_out, not_5_out);
  not not_5 (not_5_out, b);
  not not_6 (not_6_out, a);
  not not_7 (not_7_out, b);
  not not_8 (not_8_out, c);
  and and_3 (and_3_out, and_1_out, not_3_out);
  and and_4 (and_4_out, and_2_out, c);
  and and_5 (and_5_out, not_6_out, b);
  and and_6 (and_6_out, a, not_7_out);
  not not_9 (not_9_out, c);
  and and_7 (and_7_out, a, not_8_out);
  or or_1 (or_1_out, and_3_out, and_4_out);
  and and_8 (and_8_out, and_5_out, d);
  and and_9 (and_9_out, and_6_out, not_9_out);
  and and_10 (and_10_out, and_7_out, d);
  or or_2 (or_2_out, or_1_out, and_8_out);
  or or_3 (or_3_out, and_9_out, and_10_out);
  or or_4 (x, or_2_out, or_3_out);
endmodule
