// Logisim project full adder.circ as structural Verilog: 1 circuit, main circuit main
module main (
  input  A,
  input  B,
  input  Cin,
  output S,
  output Cout
);

  wire nand_1_out, nand_2_out, xor_1_out;

  xor xor_1 (xor_1_out, A, B);
  nand nand_1 (nand_1_out, xor_1_out, Cin);
  nand nand_2 (nand_2_out, A, B);
  xor xor_2 (S, xor_1_out, Cin);
  nand nand_3 (Cout, nand_1_out, nand_2_out);
endmodule
