// Logisim project jk.circ as structural Verilog: 1 circuit, main circuit main
module main (
  input  in_1,
  output out_2,
  output out_3,
  output out_4,
  output out_5
);

  wire clock_1_out, nand_1_out;

  Clock clock_1 (.out(clock_1_out));
  J_K_Flip_Flop j_k_ff_1 (
    .J(in_1), .clk(clock_1_out), .K(in_1), .Q(out_5), .reset(nand_1_out));  // open: Qn, preset, en
  J_K_Flip_Flop j_k_ff_2 (.J(in_1), .clk(out_5), .K(in_1), .Q(out_4), .reset(nand_1_out));  // open: Qn, preset, en
  J_K_Flip_Flop j_k_ff_3 (.J(in_1), .clk(out_4), .K(in_1), .Q(out_3), .reset(nand_1_out));  // open: Qn, preset, en
  J_K_Flip_Flop j_k_ff_4 (.J(in_1), .clk(out_3), .K(in_1), .Q(out_2), .reset(nand_1_out));  // open: Qn, preset, en
  nand nand_1 (nand_1_out, out_5, out_2, clock_1_out);
endmodule
