// Logisim project mini project circuit.circ as structural Verilog: 4 circuits, main circuit main
module main (
  input  in_1,
  input  in_2,
  input  in_3,
  input  in_4,
  output MOTOR,
  output out_6
);

  wire or_1_out, PB1_out, PB2_out, PB3_out;

  or PB1 (PB1_out, in_1, 1'b0);
  or PB2 (PB2_out, in_2, 1'b0);
  or PB3 (PB3_out, in_3, 1'b0);
  nand IR_SENSOR (out_6, in_4, in_4);
  or or_1 (or_1_out, PB1_out, PB2_out, PB3_out);
  and and_1 (MOTOR, or_1_out, out_6);
endmodule

module FULL_ADDER (
  input  A,
  input  B,
  input  in_3,
  output Sum,
  output Cout
);

  wire and_1_out, and_2_out, xor_1_out;

  xor xor_1 (xor_1_out, A, B);
  xor xor_2 (Sum, xor_1_out, in_3);
  and and_1 (and_1_out, xor_1_out, in_3);
  and and_2 (and_2_out, A, B);
  or or_1 (Cout, and_1_out, and_2_out);
endmodule

module PARALLER_ADD_SUB (
  input  a3,
  input  a2,
  input  a1,
  input  a0,
  input  b3,
  input  b2,
  input  b1,
  input  b0,
  input  add_sub,
  output Cout,
  output s3,
  output s2,
  output s1,
  output s0,
  output Signed_Overflow
);

  wire full_adder_2_cout, full_adder_3_cout, full_adder_4_cout, xor_2_out, xor_3_out, xor_4_out, xor_5_out;

  xor xor_1 (Signed_Overflow, Cout, full_adder_2_cout);
  xor xor_2 (xor_2_out, b3, add_sub);
  Full_adder full_adder_1 (.A(a3), .B(xor_2_out), .Cin(full_adder_2_cout), .Sum(s3), .Cout(Cout));
  xor xor_3 (xor_3_out, b2, add_sub);
  xor xor_4 (xor_4_out, b1, add_sub);
  Full_adder full_adder_2 (.A(a2), .B(xor_3_out), .Cin(full_adder_4_cout), .Sum(s2), .Cout(full_adder_2_cout));
  xor xor_5 (xor_5_out, b0, add_sub);
  Full_adder full_adder_3 (.A(a0), .B(xor_5_out), .Cin(add_sub), .Sum(s0), .Cout(full_adder_3_cout));
  Full_adder full_adder_4 (.A(a1), .B(xor_4_out), .Cin(full_adder_3_cout), .Sum(s1), .Cout(full_adder_4_cout));
endmodule

module BCD (
  input  a3,
  input  a2,
  input  a1,
  input  a0,
  input  b3,
  input  b2,
  input  b1,
  input  b0,
  input  add_sub,
  output Cout,
  output Signed_Overflow
);

  wire leda_1_x, ledb_1_x, ledc_1_x, ledd_1_x, lede_1_x, ledf_1_x, ledg_1_x,
       parallel_adder_and_subtractor_1_s0, parallel_adder_and_subtractor_1_s1,
       parallel_adder_and_subtractor_1_s2, parallel_adder_and_subtractor_1_s3;

  Parallel_adder_and_subtractor parallel_adder_and_subtractor_1 (
    .Signed_Overflow(Signed_Overflow), .Cout(Cout), .b3(b3), .a3(a3), .b2(b2), .a2(a2), .b1(b1), .a1(a1),
    .b0(b0), .a0(a0), .add_sub(add_sub), .s3(parallel_adder_and_subtractor_1_s3),
    .s2(parallel_adder_and_subtractor_1_s2), .s1(parallel_adder_and_subtractor_1_s1),
    .s0(parallel_adder_and_subtractor_1_s0));
  LEDA leda_1 (
    .a(parallel_adder_and_subtractor_1_s3), .b(parallel_adder_and_subtractor_1_s2),
    .c(parallel_adder_and_subtractor_1_s1), .d(parallel_adder_and_subtractor_1_s0), .x(leda_1_x));
  LEDB ledb_1 (
    .a(parallel_adder_and_subtractor_1_s3), .b(parallel_adder_and_subtractor_1_s2),
    .c(parallel_adder_and_subtractor_1_s1), .d(parallel_adder_and_subtractor_1_s0), .x(ledb_1_x));
  LEDC ledc_1 (
    .a(parallel_adder_and_subtractor_1_s3), .b(parallel_adder_and_subtractor_1_s2),
    .c(parallel_adder_and_subtractor_1_s1), .d(parallel_adder_and_subtractor_1_s0), .x(ledc_1_x));
  LEDD ledd_1 (
    .a(parallel_adder_and_subtractor_1_s3), .b(parallel_adder_and_subtractor_1_s2),
    .c(parallel_adder_and_subtractor_1_s1), .d(parallel_adder_and_subtractor_1_s0), .x(ledd_1_x));
  LEDE lede_1 (
    .a(parallel_adder_and_subtractor_1_s3), .b(parallel_adder_and_subtractor_1_s2),
    .c(parallel_adder_and_subtractor_1_s1), .d(parallel_adder_and_subtractor_1_s0), .x(lede_1_x));
  LEDF ledf_1 (
    .a(parallel_adder_and_subtractor_1_s3), .b(parallel_adder_and_subtractor_1_s2),
    .c(parallel_adder_and_subtractor_1_s1), .d(parallel_adder_and_subtractor_1_s0), .x(ledf_1_x));
  LEDG ledg_1 (
    .a(parallel_adder_and_subtractor_1_s3), .b(parallel_adder_and_subtractor_1_s2),
    .c(parallel_adder_and_subtractor_1_s1), .d(parallel_adder_and_subtractor_1_s0), .x(ledg_1_x));
  _7_Segment_Display u_7_segment_display_1 (
    .g(ledg_1_x), .f(ledf_1_x), .a(leda_1_x), .b(ledb_1_x), .e(lede_1_x), .d(ledd_1_x), .c(ledc_1_x));  // open: dp
endmodule
